# Fritzing sketch ttl2nim (saved by Fritzing 0.9.3b)
circuit board: 8.46667cm x 5.64444cm
breadboards: 1

parts:
  Part1 = Arduino Nano (Rev3.0)
  C1 = Ceramic Capacitor [capacitance=1nF package="100 mil [THT, multilayer]"]
  R1 = Resistor [tolerance=±5% resistance=50 package=THT]
  R2 = Resistor [tolerance=±5% resistance=50 package=THT]
  R3 = Resistor [tolerance=±5% resistance=100 package=THT]
  D1 = Rectifier Diode [part_number=1N4001 package="300 mil [THT]"]

nets:
  N1: Part1.GND, R1.Pin_0, R2.Pin_0
  N2: Part1.D2, C1.1
  N3: C1.0, R1.Pin_1, D1.cathode
  N4: R2.Pin_1, R3.Pin_0
  N5: R3.Pin_1, D1.anode
